# Fritzing sketch Sketch_Water_Mote (saved by Fritzing 0.9.3b)

parts:
  YF-S201_Flow_Meter1 = YF-S201 Water Flow Meter
  U1 = ESP8266 NodeMCU LoLin module
  OLED1 = SSD1306 0.96in 128x64 I2C Monochrome OLED Display
  SW1 = Slide_Switch_new
  JACK1 = 2.1mm Barrel Jack with Terminal Block
  S1 = Round Pushbutton

nets:
  N1: YF-S201_Flow_Meter1.SIG, U1.D7
  GND: YF-S201_Flow_Meter1.GND, U1.GND, OLED1.GND, JACK1.NEG
  N2: YF-S201_Flow_Meter1.VCC, U1.VU
  N3: U1.D1, OLED1.SCL
  N4: U1.D2, OLED1.SDA
  3V3: U1.3V3, OLED1.VCC, S1.leg1
  N5: U1.D8, S1.leg0
  N6: U1.Vin, SW1.pin_2
  N7: SW1.pin_1, JACK1.POS

notes:
  Button to switch debug mode.

custom parts:
  YF-S201 Water Flow Meter: The YF-S201 Flow Meter. The input voltage is 5V to 24V (DC).
  ESP8266 NodeMCU LoLin module: ESP8266 based NodeMCU
  Slide_Switch_new: the New two pin slide switch
