# Fritzing sketch v1 - Sketch Water_Mote (saved by Fritzing 0.9.5d)
breadboards: 1

parts:
  Part1 = LCD1602-I2C
  YF-S201_Flow_Meter1 = YF-S201 Water Flow Meter
  U1 = ESP8266 NodeMCU LoLin module

nets:
  GND: Part1.GND, YF-S201_Flow_Meter1.GND, U1.GND
  VCC: Part1.VCC, YF-S201_Flow_Meter1.VCC, U1.VU
  N1: Part1.SDA, U1.D2
  N2: Part1.SCL, U1.D1
  N3: YF-S201_Flow_Meter1.SIG, U1.D7

custom parts:
  LCD1602-I2C: A standard character display, usually with 2x16 characters. Comes in many colors with LCM1602 IIC attached.
  YF-S201 Water Flow Meter: The YF-S201 Flow Meter. The input voltage is 5V to 24V (DC).
  ESP8266 NodeMCU LoLin module: ESP8266 based NodeMCU
